# Fritzing sketch ArduinoLeonardo-fw-v180 (saved by Fritzing 0.9.3b)

parts:
  Часть2 = Arduino Leonardo (Rev3b)
  Throttle_pot = Rotary Encoder [package=THT]
  Breake_pot = Rotary Encoder [package=THT]
  Clutch_pot = Rotary Encoder [package=THT]
  Handbreake_pot = Rotary Encoder [package=THT]
  ENCODER = YumoE6B2
  Button1 = Round Pushbutton
  Button2 = Round Pushbutton
  BTS7960_(Motor_Driver) = BTS7960
  DC_MOTOR_(FFB) = DC Motor
  DC_POWER_12-24V = Power Jack [package=power_jack_slot]
  Button0 = Round Pushbutton
  Button4 = Round Pushbutton
  Button5 = Round Pushbutton
  Button6 = Round Pushbutton
  Button3 = Round Pushbutton
  FFB_Clipping_LED = LED - 5mm [color="Red (633nm)" package="5 mm [THT]"]
  R1 = Resistor [tolerance=±5% resistance=220 package=THT]  # not connected

nets:
  N1: Часть2.D0/RX, ENCODER.B
  N2: Часть2.D1/TX, ENCODER.A
  N3: Часть2.D2/SDA, ENCODER.Z
  N4: Часть2.D4/A6, Button0.leg0
  N5: Часть2.D6_PWM/A7, Button6.leg0
  N6: Часть2.D7, Button5.leg0
  N7: Часть2.5V, Throttle_pot.EncoderPinB
  N8: Часть2.GND, Throttle_pot.EncoderPinA
  N9: Часть2.A0, Throttle_pot.EncoderPinC
  N10: Часть2.A1, Breake_pot.EncoderPinC
  N11: Часть2.A2, Clutch_pot.EncoderPinC
  N12: Часть2.A3, Handbreake_pot.EncoderPinC
  N13: Часть2.A4, Button2.leg0
  N14: Часть2.A5, Button1.leg0
  N15: Часть2.D8/A8, Button4.leg0
  N16: Часть2.D9_PWM/A9, BTS7960_(Motor_Driver).pin2
  N17: Часть2.D10_PWM/A10, BTS7960_(Motor_Driver).pin1
  N18: Часть2.D12/A11, Button3.leg0
  N19: Часть2.D13_PWM, FFB_Clipping_LED.anode
  N20: BTS7960_(Motor_Driver).pin3, BTS7960_(Motor_Driver).pin4
  N21: BTS7960_(Motor_Driver).pin9, DC_MOTOR_(FFB).pin_2
  N22: BTS7960_(Motor_Driver).pin10, DC_MOTOR_(FFB).pin_1
  N23: BTS7960_(Motor_Driver).pin11, DC_POWER_12-24V.PWR
  N24: BTS7960_(Motor_Driver).pin12, DC_POWER_12-24V.GND

notes:
  z-index supported in fw version with "z" option only (fw-v18Xz)
  +
  220Ω-680Ω
  PWM direction
  -
  PWM direction - only for pwm+dir mode of FFB output.

custom parts:
  YumoE6B2: Yumo E6B2-C incremental encoder. Resolutions 10 to 4000 pulses per revolution (depending on model number). Power from 5 to 24V (again depending on model). Dia 40mm body 30mm plus 20mm shaft.
  BTS7960: BTS7960 43A Peak Power H-Bridge PWM Motor Driver
