# Fritzing sketch ArduinoLeonardo-fw-v182-LC (saved by Fritzing 0.9.3b)

parts:
  Часть2 = Arduino Leonardo (Rev3b)
  Throttle_pot = Rotary Encoder [package=THT]
  Clutch_pot = Rotary Encoder [package=THT]
  Handbreake_pot = Rotary Encoder [package=THT]
  HX711_(Load_Cell_Amplifer) = HX711 Weighing Sensor Module  # not connected
  Load_Cell_(Weight_Sensors) = Load Cell - Red/white/black/green  # not connected
  Button0 = Round Pushbutton

nets:
  N1: Часть2.5V, Throttle_pot.EncoderPinB
  N2: Часть2.GND, Throttle_pot.EncoderPinA
  N3: Часть2.A0, Throttle_pot.EncoderPinC
  N4: Часть2.A1, Clutch_pot.EncoderPinC
  N5: Часть2.A2, Handbreake_pot.EncoderPinC
  N6: Часть2.A3, Button0.leg1

notes:
  VCC
  SCK (CLOCK)
  DT (DATA)
  GND
  A-
  A+
  E-
  E+
  Only for wirmware with option fw-v182
  Other connections as in fw-v180

custom parts:
  Load Cell - Red/white/black/green: A rectangle load cell/weighting pressure Sensor with four wires - Red, white, black, green. Normally corresponding with E+, E-, A+, A- respectively.
