# Fritzing sketch ArduinoLeonardo-fw-v183-DAC (saved by Fritzing 0.9.3b)

parts:
  Arduino_Leonardo_Micro_or_ProMicro = Arduino Leonardo (Rev3b)
  DAC1_0x61_right = Adafruit MCP4725 Breakout Board - 12-Bit DAC [part_number=MCP4725]
  DAC1_0x62_left = Adafruit MCP4725 Breakout Board - 12-Bit DAC [part_number=MCP4725]
  IC1 = TL072 [package="DIP (Dual Inline) [THT]"]
  Компонент1 = TL072 [package="DIP (Dual Inline) [THT]"]  # not connected
  IC1_1 = TL072 [package="DIP (Dual Inline) [THT]"]  # not connected
  IC1_2 = TL072 [package="DIP (Dual Inline) [THT]"]  # not connected
  R1 = Resistor [tolerance=±5% resistance=10k package=THT]
  R2 = Resistor [tolerance=±5% resistance=10k package=THT]
  R3 = Resistor [tolerance=±5% resistance=20k package=THT]
  R4 = Resistor [tolerance=±5% resistance=20k package=THT]

nets:
  N1: Arduino_Leonardo_Micro_or_ProMicro.D2/SDA, DAC1_0x62_left.SDA
  N2: Arduino_Leonardo_Micro_or_ProMicro.D3_PWM/SCL, DAC1_0x62_left.SCL
  5V: Arduino_Leonardo_Micro_or_ProMicro.5V, DAC1_0x62_left.VDD
  GND: Arduino_Leonardo_Micro_or_ProMicro.GND, DAC1_0x62_left.GND
  N3: DAC1_0x61_right.VOUT, R2.Pin_1
  N4: DAC1_0x62_left.VOUT, R1.Pin_1
  N5: IC1.connector1, R1.Pin_0, R4.Pin_1
  N6: IC1.connector2, R2.Pin_0, R3.Pin_0

notes:
  V++
  V--
  Output ±10V
  -
  +
  Shielded audio grade cable
  Shielded audio grade cable
  must be grounded
  VCC can be provided by regulated bipolar power supply use LM7812, LM7912 for ±12V or LM7815, LM7915 for ±15V
  Goes to AASD analog input use of analog optocoupler is desired but not required
  IC1 -can be any audio grade operational amplifier like TL072, NE5532 or equivalent
  DAC0 - ADDR pin to GND i2C address 0x60 is for left force
  DAC1 - ADDR pin to VCC i2C address 0x61 is for right force

custom parts:
  Adafruit MCP4725 Breakout Board - 12-Bit DAC: Your microcontroller probably has an ADC (analog -> digital converter) but does it have a DAC (digital -> analog converter)??? Now it can! This breakout board features the easy-to-use MCP4725 12-bit DAC. Control it via I2C and send it the value you want it to output, and the VOUT pin will have it. Great for audio / analog projects, such as when you can't use PWM but need a sine wave or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
  TL072: Dual Operational Amplifier
  TL072: Dual Operational Amplifier
  TL072: Dual Operational Amplifier
  TL072: Dual Operational Amplifier
