# Fritzing sketch ArduinoLeonardo-fw-v18Xs-ads1015 (saved by Fritzing 0.9.3b)

parts:
  Arduino_Leonardo_Micro_or_ProMicro = Arduino Leonardo (Rev3b)
  Throttle_pot = Rotary Encoder [package=THT]
  Breake_pot = Rotary Encoder [package=THT]
  Clutch_pot = Rotary Encoder [package=THT]
  Handbreake_pot = Rotary Encoder [package=THT]
  ads1015_or_ads1115 = ADS1115

nets:
  N1: Arduino_Leonardo_Micro_or_ProMicro.D2/SDA, ads1015_or_ads1115.SDA
  N2: Arduino_Leonardo_Micro_or_ProMicro.D3_PWM/SCL, ads1015_or_ads1115.SCL
  N3: Arduino_Leonardo_Micro_or_ProMicro.5V, Throttle_pot.EncoderPinB
  N4: Arduino_Leonardo_Micro_or_ProMicro.GND, Throttle_pot.EncoderPinA
  N5: Throttle_pot.EncoderPinC, ads1015_or_ads1115.A0
  N6: Breake_pot.EncoderPinC, ads1015_or_ads1115.A1
  N7: Clutch_pot.EncoderPinC, ads1015_or_ads1115.A2
  N8: Handbreake_pot.EncoderPinC, ads1015_or_ads1115.A3

notes:
  10K liner pots
  Only for wirmware with option "s" (fw-v18Xs)
  Other connections as in fw-v180
  ADS1015 gain in the firmware is set to 4.099V so you have to be careful not to move the port wiper more than 4.1V in order to avoid damaging ADC.
  You may set ADDR pin to GND in order to make sure that ADC gets i2C address 0x48 witches by firmware.

custom parts:
  ADS1115: ADC ADS1115
