# Fritzing sketch ArduinoLeonardoSketch (saved by Fritzing 0.9.3b)

parts:
  Часть2 = Arduino Leonardo (Rev3b)
  Throttle_pot = Rotary Encoder [package=THT]
  Breake_pot_(if_LC*_-_then_clutch_pot) = Rotary Encoder [package=THT]
  Clutch_pot_(if_LC*_-_then_handbreake_pot) = Rotary Encoder [package=THT]
  Handbreake_pot_(if_LC*_-_then_botton0) = Rotary Encoder [package=THT]
  ENCODER = YumoE6B2
  Button_3 = Round Pushbutton
  Button_4 = Round Pushbutton
  Load_Cell_Amplifer = HX711 Weighing Sensor Module  # not connected
  Load_Cell_(Weight_Sensors) = Load Cell - Red/white/black/green  # not connected
  BTS7960_(Motor_Driver) = BTS7960
  DC_MOTOR_(FFB) = DC Motor
  DC_POWER_12-24V = Power Jack [package=power_jack_slot]
  Button_0 = Round Pushbutton  # not connected
  Button4 = Round Pushbutton  # not connected
  Button5 = Round Pushbutton  # not connected
  Button6 = Round Pushbutton  # not connected
  Leonardo_Nano_(Shift_register_for_button_box) = Arduino Nano (Rev3.0)  # not connected

nets:
  N1: Часть2.D0/RX, ENCODER.B
  N2: Часть2.D1/TX, ENCODER.A
  N3: Часть2.D2/SDA, ENCODER.Z
  N4: Часть2.5V, Throttle_pot.EncoderPinB
  N5: Часть2.GND, Throttle_pot.EncoderPinA
  N6: Часть2.A0, Throttle_pot.EncoderPinC
  N7: Часть2.A1, Breake_pot_(if_LC*_-_then_clutch_pot).EncoderPinC
  N8: Часть2.A2, Clutch_pot_(if_LC*_-_then_handbreake_pot).EncoderPinC
  N9: Часть2.A3, Handbreake_pot_(if_LC*_-_then_botton0).EncoderPinC
  N10: Часть2.A4, Button_4.leg0
  N11: Часть2.A5, Button_3.leg0
  N12: Часть2.D9_PWM/A9, BTS7960_(Motor_Driver).pin2
  N13: Часть2.D10_PWM/A10, BTS7960_(Motor_Driver).pin1
  N14: Часть2.D11_PWM, BTS7960_(Motor_Driver).pin3, BTS7960_(Motor_Driver).pin4
  N15: BTS7960_(Motor_Driver).pin9, DC_MOTOR_(FFB).pin_2
  N16: BTS7960_(Motor_Driver).pin10, DC_MOTOR_(FFB).pin_1
  N17: BTS7960_(Motor_Driver).pin11, DC_POWER_12-24V.PWR
  N18: BTS7960_(Motor_Driver).pin12, DC_POWER_12-24V.GND

notes:
  Button 1,2 (fw-v180 only)
  LC* - load cell with HX711 (fw-w182)
  VCC
  SCK (CLOCK)
  DT (DATA)
  GND
  XH711 (fw-v182 only) or button0
  A-
  A+
  E-
  E+
  OR*
  OR* - connection differences for the firmware version.

custom parts:
  YumoE6B2: Yumo E6B2-C incremental encoder. Resolutions 10 to 4000 pulses per revolution (depending on model number). Power from 5 to 24V (again depending on model). Dia 40mm body 30mm plus 20mm shaft.
  Load Cell - Red/white/black/green: A rectangle load cell/weighting pressure Sensor with four wires - Red, white, black, green. Normally corresponding with E+, E-, A+, A- respectively.
  BTS7960: BTS7960 43A Peak Power H-Bridge PWM Motor Driver
