# Fritzing sketch ArduinoNanoOrUno-button-box (saved by Fritzing 0.9.3b)

parts:
  Arduino_Nano/Uno = Arduino Nano (Rev3.0)
  Up = Round Pushbutton
  Button7 = Round Pushbutton
  Left = Round Pushbutton
  Button8 = Round Pushbutton
  Button11 = Round Pushbutton
  Right = Round Pushbutton
  Button1 = Round Pushbutton
  Down = Round Pushbutton
  Button10 = Round Pushbutton
  Button9 = Round Pushbutton
  Button3 = Round Pushbutton
  Arduino_Leonardo_Micro_or_ProMicro = Arduino Leonardo (Rev3b)
  Button5 = Round Pushbutton
  Button6 = Round Pushbutton
  Button2 = Round Pushbutton
  Button4 = Round Pushbutton
  button12 = Round Pushbutton

nets:
  N1: Arduino_Nano/Uno.D1/TX, Button7.leg0
  N2: Arduino_Nano/Uno.D0/RX, Button8.leg0
  N3: Arduino_Nano/Uno.D2, Arduino_Leonardo_Micro_or_ProMicro.D8/A8
  N4: Arduino_Nano/Uno.D3, Button1.leg0
  N5: Arduino_Nano/Uno.D4, Button9.leg0
  N6: Arduino_Nano/Uno.D5, button12.leg0
  N7: Arduino_Nano/Uno.D6, Button4.leg0
  N8: Arduino_Nano/Uno.D7, Button6.leg0
  N9: Arduino_Nano/Uno.D8, Button2.leg0
  N10: Arduino_Nano/Uno.D9, Button5.leg0
  N11: Arduino_Nano/Uno.D11/MOSI, Button3.leg0
  N12: Arduino_Nano/Uno.D12/MISO, Arduino_Leonardo_Micro_or_ProMicro.D6_PWM/A7
  GND: Arduino_Nano/Uno.GND, Arduino_Leonardo_Micro_or_ProMicro.GND
  5V: Arduino_Nano/Uno.5V, Arduino_Leonardo_Micro_or_ProMicro.5V
  N13: Arduino_Nano/Uno.A5, Button11.leg0
  N14: Arduino_Nano/Uno.A4, Button10.leg0
  N15: Arduino_Nano/Uno.A3, Down.leg0
  N16: Arduino_Nano/Uno.A2, Right.leg0
  N17: Arduino_Nano/Uno.A1, Left.leg0
  N18: Arduino_Nano/Uno.A0, Up.leg0
  N19: Arduino_Nano/Uno.D13/SCK, Arduino_Leonardo_Micro_or_ProMicro.D7

notes:
  DT
  CLK
  PL
  This pinout is valid for firmware fw-vXX1, fw-vXX2 only. Max 16 buttons. Other connections as in fw-v180
  A (button 6) -> pin 7 (portD bit7)
  B (button 4) -> pin 6 (portD bit6)
  RS (button 12) -> pin 5 (portD bit5)
  Menu (button 9) -> pin 4 (portD bit4)
  Gear Down (button 1 = L_Pad) -> pin 3 (portD bit3)
  X (button 5) -> pin 9 (portB bit1)
  Manettino CCW (button 7, View) -> pin 1 (portD bit1) - if you don't use serial debug (UART TX)
  Manettino CW (button 8, Menu) -> pin 0 (portD bit0) - if you don't use serial debug (UART RX)
  Gear Up (button 2 = R_Pad) -> pin 8 (portB bit0)
  Y (button 3) -> pin 11 (portB bit3)
  LS (button 11) -> pin A5 (portC bit5)
  View (button 10 – under X) -> pin A4 (portC bit4)
  D-Pad Down -> pin A3 (portC bit3)
  D-Pad Right -> pin A2 (portC bit2)
  D-Pad Left -> pin A1 (portC bit1)
  D-Pad Up -> pin A0 (portC bit0)
  Goes in the wheel rim along with all switches up to 16 switches are possible (can be less or none)
  You will need to find a way to take 5 wires through or around the wheel shaft.
  Other connections as in fw-v180
