# Fritzing sketch ArduinoProMicro-fw-v180m (saved by Fritzing 0.9.3b)

parts:
  Часть1 = Arduino Pro Micro (Clone)
  BTS7960_(FFB_Motor_Driver) = BTS7960
  FFB_Clipping_LED = LED - 5mm [color="Red (633nm)" package="5 mm [THT]"]
  Button1 = Round Pushbutton
  Button2 = Round Pushbutton
  Button3 = Round Pushbutton
  R2 = Resistor [tolerance=±5% resistance=220 package=THT]
  ENCODER = YumoE6B2

nets:
  N1: Часть1.TXO, ENCODER.B
  N2: Часть1.RXI, ENCODER.A
  N3: Часть1.D2, Button3.leg0
  N4: Часть1.D3, FFB_Clipping_LED.anode
  N5: Часть1.D9, BTS7960_(FFB_Motor_Driver).pin2
  N6: Часть1.D10, BTS7960_(FFB_Motor_Driver).pin1
  N7: Часть1.D14, Button1.leg0
  N8: Часть1.D15, Button2.leg0
  N9: Часть1.VCC, BTS7960_(FFB_Motor_Driver).pin7
  N10: Часть1.GND, BTS7960_(FFB_Motor_Driver).pin8
  N11: BTS7960_(FFB_Motor_Driver).pin3, BTS7960_(FFB_Motor_Driver).pin4
  N12: FFB_Clipping_LED.cathode, R2.Pin_1

notes:
  +
  220Ω-680Ω
  Other connections as in fw-v180
  PWM direction
  PWM direction - only for pwm+dir mode of FFB output.

custom parts:
  BTS7960: BTS7960 43A Peak Power H-Bridge PWM Motor Driver
  YumoE6B2: Yumo E6B2-C incremental encoder. Resolutions 10 to 4000 pulses per revolution (depending on model number). Power from 5 to 24V (again depending on model). Dia 40mm body 30mm plus 20mm shaft.
