# Fritzing sketch ArduinoProMicro-fw-v180zm (saved by Fritzing 0.9.3b)

parts:
  Часть1 = Arduino Pro Micro (Clone)
  ENCODER = YumoE6B2

nets:
  N1: Часть1.TXO, ENCODER.B
  N2: Часть1.RXI, ENCODER.A
  N3: Часть1.D2, ENCODER.Z
  N4: Часть1.VCC, ENCODER.V
  GND: Часть1.GND, ENCODER.GND

notes:
  z-index supported in fw version with "z" option only (fw-v18Xz)
  Other connections as in fw-v180

custom parts:
  YumoE6B2: Yumo E6B2-C incremental encoder. Resolutions 10 to 4000 pulses per revolution (depending on model number). Power from 5 to 24V (again depending on model). Dia 40mm body 30mm plus 20mm shaft.
