# Fritzing sketch ArduinoProMicro-fw-v18Xm (saved by Fritzing 0.9.3b)

parts:
  Часть1 = Arduino Pro Micro (Clone)
  BTS7960_(FFB_Motor_Driver) = BTS7960
  FFB_Clipping_LED = LED - 5mm [color="Red (633nm)" package="5 mm [THT]"]
  Button1 = Round Pushbutton
  Button2 = Round Pushbutton
  Button3 = Round Pushbutton

nets:
  N1: Часть1.D2, Button3.leg0
  N2: Часть1.D3, FFB_Clipping_LED.anode
  N3: Часть1.D9, BTS7960_(FFB_Motor_Driver).pin2
  N4: Часть1.D10, BTS7960_(FFB_Motor_Driver).pin1
  N5: Часть1.D16, BTS7960_(FFB_Motor_Driver).pin3, BTS7960_(FFB_Motor_Driver).pin4
  N6: Часть1.D14, Button1.leg0
  N7: Часть1.D15, Button2.leg0
  N8: Часть1.VCC, BTS7960_(FFB_Motor_Driver).pin7
  N9: Часть1.GND, BTS7960_(FFB_Motor_Driver).pin8

notes:
  +

custom parts:
  BTS7960: BTS7960 43A Peak Power H-Bridge PWM Motor Driver
